// Logisim project regfile.circ as structural Verilog: 1 circuit, main circuit main
module main (
  input  [3:0] Read_Register_1,
  input  [3:0] Read_Register_2,
  input  [3:0] Write_Register,
  input  [31:0] Write_Data,
  input  Write_Enable,
  input  Clock,
  input  [31:0] R15,
  output [31:0] R0_Value,
  output [31:0] R1_Value,
  output [31:0] R3_Value,
  output [31:0] LR__R14__Value,
  output [31:0] SP__R13__Value,
  output [31:0] Read_Data_1,
  output [31:0] Read_Data_2
);

  wire and_1_out, comparator_1_eq, comparator_2_eq, comparator_3_eq, comparator_4_eq, comparator_5_eq,
       registerfile_1_p1, registerfile_1_p2, registerfile_1_p4, registerfile_1_p6, registerfile_2_p1,
       registerfile_2_p4, registerfile_2_p8, registerfile_2_p14, registerfile_2_p16, registerfile_3_p5,
       registerfile_4_p6;
  wire [31:0] multiplexer_1_out, multiplexer_2_out, R15Value, registerfile_2_p12, registerfile_2_p13;

  Comparator #(.width(4)) comparator_1 (.a(4'b0000), .b(Write_Register), .eq(comparator_1_eq));  // open: gt, lt
  and and_1 (and_1_out, comparator_1_eq, Write_Enable);
  Register #(.width(32)) register_1 (.D(R15), .Q(R15Value), .clk(Clock));  // open: en, clr
  Register #(.width(32)) register_2 (.D(Write_Data), .en(and_1_out), .Q(R0_Value), .clk(Clock));  // open: clr
  // RegisterFile registerfile_1: pin names not known; wires that end beside it: registerfile_1_p1, registerfile_1_p2, registerfile_1_p2, registerfile_1_p4, registerfile_1_p4, registerfile_1_p6, Write_Data, Clock, Write_Register, Write_Enable, {1'b0, Write_Register}, 5'b01101, 5'b01110, SP__R13__Value, LR__R14__Value
  // RegisterFile registerfile_2: pin names not known; wires that end beside it: registerfile_2_p1, Write_Data, Clock, registerfile_2_p4, Write_Enable, registerfile_2_p4, {1'b0, Write_Register}, registerfile_2_p8, {1'b0, Read_Register_1}, {1'b0, Read_Register_2}, registerfile_2_p8, registerfile_2_p12, registerfile_2_p13, registerfile_2_p14, registerfile_2_p14, registerfile_2_p16, registerfile_2_p16, registerfile_2_p1
  Comparator #(.width(4)) comparator_2 (.a(4'b0000), .b(Read_Register_1), .eq(comparator_2_eq));  // open: gt, lt
  Comparator #(.width(4)) comparator_3 (.a(4'b1111), .b(Read_Register_1), .eq(comparator_3_eq));  // open: gt, lt
  // RegisterFile registerfile_3: pin names not known; wires that end beside it: Write_Data, Clock, Write_Enable, {1'b0, Write_Register}, registerfile_3_p5, registerfile_3_p5, 5'b00001, R1_Value
  Multiplexer #(.width(32), .enable("false")) multiplexer_1 (
    .in0(registerfile_2_p12), .in1(R15Value), .out(multiplexer_1_out), .sel(comparator_3_eq));
  Multiplexer #(.width(32), .enable("false")) multiplexer_2 (
    .in0(registerfile_2_p13), .in1(R15Value), .out(multiplexer_2_out), .sel(comparator_4_eq));
  Comparator #(.width(4)) comparator_4 (.a(4'b1111), .b(Read_Register_2), .eq(comparator_4_eq));  // open: gt, lt
  Comparator #(.width(4)) comparator_5 (.a(4'b0000), .b(Read_Register_2), .eq(comparator_5_eq));  // open: gt, lt
  Multiplexer #(.width(32), .enable("false")) multiplexer_3 (
    .in0(multiplexer_1_out), .in1(R0_Value), .out(Read_Data_1), .sel(comparator_2_eq));
  Multiplexer #(.width(32), .enable("false")) multiplexer_4 (
    .in0(multiplexer_2_out), .in1(R0_Value), .out(Read_Data_2), .sel(comparator_5_eq));
  // RegisterFile registerfile_4: pin names not known; wires that end beside it: Write_Data, Clock, Write_Enable, {1'b0, Write_Register}, 5'b00010, registerfile_4_p6, registerfile_4_p6, R3_Value

  // Other names for the same wires on the sheet: read_reg1[3:0] = Read_Register_1; read_reg2[3:0] = Read_Register_2;
  //   write_reg[3:0] = Write_Register; clk = Clock; lr[31:0] = LR__R14__Value; r1[31:0] = R1_Value;
  //   r2[31:0] = R3_Value; sp[31:0] = SP__R13__Value; write_en = Write_Enable

  // Notes on the sheet:
  //   INPUTS to your circuit
  //   DON'T CHANGE THE LOCATIONS OF THE INPUTS AND OUTPUTS!
  //   PC+8 (R15) really lives here
  //   R0 really lives here
  //   These are DEBUG/TEST outputs from your circuit.
  //   copies
  //   OUTPUTS from your circuit
endmodule
