// Logisim project alu-control-ldr-str-test.circ as structural Verilog: 1 circuit, main circuit main
module main (
  output [7:0] Test_num,
  output halt,
  output [3:0] ALUControl
);

  wire clock_1_out;
  wire [1:0] rom_1_data, rom_5_data;
  wire [3:0] rom_3_data;
  wire [5:0] rom_4_data;
  wire [7:0] adder_1_out;

  Clock clock_1 (.out(clock_1_out));
  Adder adder_1 (.a(8'h1), .b(Test_num), .out(adder_1_out));  // open: cin, cout
  Register register_1 (.D(adder_1_out), .Q(Test_num), .clk(clock_1_out));  // open: en, clr
  Comparator #(.mode("unsigned")) comparator_1 (.a(8'hf), .b(Test_num), .eq(halt));  // open: gt, lt
  ROM #(.dataWidth(2)) rom_1 (.addr(Test_num), .data(rom_1_data));  // open: sel
  ROM #(.dataWidth(1)) rom_2 (.addr(Test_num), .data(rom_4_data[5]));  // open: sel
  ROM #(.dataWidth(4)) rom_3 (.addr(Test_num), .data(rom_3_data));  // open: sel
  ROM #(.dataWidth(1)) rom_4 (.addr(Test_num), .data(rom_4_data[0]));  // open: sel
  ROM #(.dataWidth(2)) rom_5 (.addr(Test_num), .data(rom_5_data));  // open: sel
  // alu_control_main main_1: pin names not known; wires that end beside it: rom_1_data, {rom_4_data[5], rom_3_data, rom_4_data[0]}, rom_5_data, ALUControl

  // Notes on the sheet:
  //   contents of rom_1 (hex, n*v repeats v):
  //   4*1
  //   funct
  //   ~I
  //   contents of rom_2 (hex, n*v repeats v):
  //   0 0 1 1
  //   PUBW
  //   L
  //   contents of rom_4 (hex, n*v repeats v):
  //   0 1 0 1
  //   There should be no blue/red wires here, and the result shouldn't be x's.
  //   op (00=data, 01=ldr/str, 10=branch)
  //   sh (00=lsl, 01=lsr, 10=asr)
endmodule
